// Logisim project Barbusoft.circ as structural Verilog: 4 circuits, main circuit main
module main (
);

  wire and_1_out, and_2_out, clock_1_out, not_1_out;
  wire [7:0] alu_1_address, alu_1_aluout, Data_Memory_dout, multiplexer_1_out, multiplexer_2_out,
       register_bank_1_regdata1, register_bank_1_regdata2, register_bank_1_regdata3;
  wire [15:0] instruction_register_1_ramread;

  Clock clock_1 (.out(clock_1_out));
  Instruction_Register instruction_register_1 (.Clock(clock_1_out), .RamRead(instruction_register_1_ramread));
  not not_1 (not_1_out, instruction_register_1_ramread[14]);
  and and_1 (and_1_out, not_1_out, instruction_register_1_ramread[15]);
  Multiplexer #(.width(8)) multiplexer_1 (
    .in0(alu_1_aluout), .in1(Data_Memory_dout), .out(multiplexer_1_out),
    .sel(instruction_register_1_ramread[11]));
  and and_2 (and_2_out, instruction_register_1_ramread[10], instruction_register_1_ramread[11]);
  RAM #(.trigger("falling")) Data_Memory (
    .addr(alu_1_address), .we(and_2_out), .oe(1'b1), .clk(clock_1_out), .din(alu_1_aluout),
    .dout(Data_Memory_dout));
  Multiplexer #(.width(8)) multiplexer_2 (
    .in0(multiplexer_2_out), .in1(alu_1_aluout), .out(multiplexer_2_out),
    .sel(instruction_register_1_ramread[14]));
  Hex_Digit_Display #(.decimalPoint("false")) hex_digit_display_1 (.value(multiplexer_2_out[7:4]));
  Hex_Digit_Display #(.decimalPoint("false")) hex_digit_display_2 (.value(multiplexer_2_out[3:0]));
  Register_Bank register_bank_1 (
    .WriteReg(instruction_register_1_ramread[1:0]), .RegWrite(and_1_out), .RegDataW(multiplexer_1_out),
    .ReadReg1(instruction_register_1_ramread[5:4]), .ReadReg2(instruction_register_1_ramread[3:2]),
    .ReadReg3(instruction_register_1_ramread[1:0]), .Clock(clock_1_out), .RegData1(register_bank_1_regdata1),
    .RegData2(register_bank_1_regdata2), .RegData3(register_bank_1_regdata3));
  ALU alu_1 (
    .Rn(register_bank_1_regdata1), .Rm(register_bank_1_regdata2),
    .Immediate(instruction_register_1_ramread[9:6]), .Rd(register_bank_1_regdata3),
    .InstructType(instruction_register_1_ramread[11]), .InstructChoose(instruction_register_1_ramread[10]),
    .IMM(instruction_register_1_ramread[12]), .SET(instruction_register_1_ramread[13]),
    .AluOut(alu_1_aluout), .Address(alu_1_address));

  // Notes on the sheet:
  //   Jacob Barbulescu
  //   The Barbusoft 9000
  //   I pledge my Honor that I have abided by the Stevens Honor System.
  //   Data Memory
  //   Shows value of Rd
endmodule

module Register_Bank (
  input  [1:0] WriteReg,
  input  RegWrite,
  input  [7:0] RegDataW,
  input  [1:0] ReadReg1,
  input  [1:0] ReadReg2,
  input  [1:0] ReadReg3,
  input  Clock,
  output [7:0] RegData1,
  output [7:0] RegData2,
  output [7:0] RegData3
);

  wire and_1_out, and_2_out, and_3_out, and_4_out, decoder_1_out0, decoder_1_out1, decoder_1_out2,
       decoder_1_out3;
  wire [7:0] X0_q, X1_q, X2_q, X3_q;

  Decoder #(.select(2)) decoder_1 (
    .out0(decoder_1_out0), .out1(decoder_1_out1), .out2(decoder_1_out2), .out3(decoder_1_out3), .sel(WriteReg));  // open: en
  and and_1 (and_1_out, decoder_1_out0, RegWrite);
  Register X0 (.D(RegDataW), .en(and_1_out), .clk(Clock), .Q(X0_q));  // open: clr
  and and_2 (and_2_out, decoder_1_out1, RegWrite);
  and and_3 (and_3_out, decoder_1_out2, RegWrite);
  Register X1 (.D(RegDataW), .en(and_2_out), .clk(Clock), .Q(X1_q));  // open: clr
  and and_4 (and_4_out, decoder_1_out3, RegWrite);
  Register X2 (.D(RegDataW), .en(and_3_out), .clk(Clock), .Q(X2_q));  // open: clr
  Multiplexer #(.select(2), .width(8)) multiplexer_1 (
    .in0(X0_q), .in1(X1_q), .in2(X2_q), .in3(X3_q), .out(RegData3), .sel(ReadReg3));
  Multiplexer #(.select(2), .width(8)) multiplexer_2 (
    .in0(X0_q), .in1(X1_q), .in2(X2_q), .in3(X3_q), .out(RegData1), .sel(ReadReg1));
  Multiplexer #(.select(2), .width(8)) multiplexer_3 (
    .in0(X0_q), .in1(X1_q), .in2(X2_q), .in3(X3_q), .out(RegData2), .sel(ReadReg2));
  Register X3 (.D(RegDataW), .en(and_4_out), .clk(Clock), .Q(X3_q));  // open: clr

  // Notes on the sheet:
  //   Jacob Barbulescu. I pledge my Honor that I have abided by the Stevens Honor System
endmodule

module ALU (
  input  [7:0] Rn,
  input  [7:0] Rm,
  input  [3:0] Immediate,
  input  [7:0] Rd,
  input  InstructType,
  input  InstructChoose,
  input  IMM,
  input  SET,
  output [7:0] AluOut,
  output [7:0] Address
);

  wire [7:0] multiplexer_1_out, multiplexer_2_out, multiplexer_3_out, subtractor_1_out;

  Multiplexer #(.width(8)) multiplexer_1 (.in0(Rm), .in1({4'b0000, Immediate}), .out(multiplexer_1_out), .sel(IMM));
  Adder adder_1 (.a(Rn), .b(multiplexer_1_out), .out(Address));  // open: cin, cout
  Subtractor subtractor_1 (.a(Rn), .b(multiplexer_1_out), .out(subtractor_1_out));  // open: bin, bout
  Multiplexer #(.width(8)) multiplexer_2 (
    .in0(Address), .in1(subtractor_1_out), .out(multiplexer_2_out), .sel(InstructChoose));
  Multiplexer #(.width(8)) multiplexer_3 (
    .in0(multiplexer_2_out), .in1(Rd), .out(multiplexer_3_out), .sel(InstructType));
  Multiplexer #(.width(8)) multiplexer_4 (.in0(multiplexer_3_out), .in1(multiplexer_1_out), .out(AluOut), .sel(SET));

  // Notes on the sheet:
  //   Rm/Immediate
  //   Add/Sub
  //   Add/Ldr
  //   Set
endmodule

module Instruction_Register (
  input  Clock,
  output [15:0] RamRead
);

  wire [7:0] adder_1_out, PC_q;

  Register #(.trigger("falling")) PC (.D(adder_1_out), .en(1'b1), .clk(Clock), .Q(PC_q));  // open: clr
  RAM #(.dataWidth(16)) Memory (.addr(PC_q), .we(1'b0), .oe(1'b1), .clk(Clock), .dout(RamRead));  // open: din
  Adder adder_1 (.a(PC_q), .b({{7{1'b0}}, RamRead[15]}), .out(adder_1_out));  // open: cin, cout

  // Notes on the sheet:
  //   Jacob Barbulescu I pledge by Honor that I have abided by the Stevens Honor System.
endmodule
